# Fritzing sketch YiMultiRemote (saved by Fritzing 0.9.3b)
breadboards: 1

parts:
  WeMos_D1_Mini1 = WeMos D1 Mini
  Switch = Round Pushbutton
  5V = Power plug
  Buzzer = Piezo Buzzer
  R1 = Resistor [tolerance=±5% resistance=68 package=THT]
  LED = smd LED [color="Red (633nm)" package="0805 [SMD]"]

nets:
  N1: WeMos_D1_Mini1.3V3, R1.Pin_0
  5V: WeMos_D1_Mini1.5V, 5V.VCC
  N2: WeMos_D1_Mini1.D5, Buzzer.pin_2
  N3: WeMos_D1_Mini1.D6, LED.cathode
  N4: WeMos_D1_Mini1.D7, Switch.leg0
  N5: WeMos_D1_Mini1.G, Switch.leg1, 5V.GND, Buzzer.pin_1
  N6: R1.Pin_1, LED.anode

custom parts:
  Piezo Buzzer: Piezo buzzer PS1420P02CT
